// Logisim project TrabalhoFinalSistemasDigitais.circ as structural Verilog: 3 circuits, main circuit main
module main (
  input  [15:0] A,
  input  [15:0] B,
  input  LH,
  input  [15:0] C,
  input  [1:0] M1,
  input  clkH,
  input  RSTH,
  input  [1:0] M0,
  input  H,
  input  [7:0] X,
  input  LS,
  input  LX,
  input  clkS,
  input  [1:0] M2,
  input  RST,
  output [15:0] out_16,
  output [15:0] Pronto,
  output [15:0] out_18
);

  wire clk_out;
  wire [7:0] R0_q;
  wire [15:0] multiplexer_1_out, multiplexer_2_out, multiplexer_3_out, somadormultiplicador_1_out_4;

  Register R0 (.D(X), .en(LX), .clk(clk_out), .Q(R0_q), .clr(RST));
  Clock clk (.out(clk_out));
  Multiplexer #(.enable("false"), .select(2), .width(16)) multiplexer_1 (
    .in1(A), .in2(B), .in3(C), .out(multiplexer_1_out), .sel(M0));  // open: in0
  assign out_18 = {{8{R0_q[7]}}, R0_q};  // Bit_Extender bit_extender_1
  Multiplexer #(.enable("false"), .select(2), .width(16)) multiplexer_2 (
    .in0(multiplexer_1_out), .in1(out_18), .in2(Pronto), .in3(out_16), .out(multiplexer_2_out), .sel(M1));
  Multiplexer #(.enable("false"), .select(2), .width(16)) multiplexer_3 (
    .in0(out_18), .in1(multiplexer_1_out), .in2(Pronto), .in3(out_16), .out(multiplexer_3_out), .sel(M2));
  SomadorMultiplicador somadormultiplicador_1 (
    .ABC(multiplexer_2_out), .X(multiplexer_3_out), .H(H), .out_4(somadormultiplicador_1_out_4));
  Register #(.width(16)) R1 (.D(somadormultiplicador_1_out_4), .en(LH), .clk(clkH), .Q(out_16), .clr(RSTH));
  Register #(.width(16)) R2 (.D(somadormultiplicador_1_out_4), .en(LS), .clk(clkS), .Q(Pronto));  // open: clr
endmodule

module SomadorMultiplicador (
  input  [15:0] ABC,
  input  [15:0] X,
  input  H,
  output [15:0] out_4
);

  wire [15:0] adder_1_out, multiplier_1_out;

  Multiplier #(.width(16)) multiplier_1 (.a(ABC), .b(X), .out(multiplier_1_out));  // open: cin, cout
  Adder #(.width(16)) adder_1 (.a(ABC), .b(X), .out(adder_1_out));  // open: cin, cout
  Multiplexer #(.enable("false"), .width(16)) multiplexer_1 (
    .in0(adder_1_out), .in1(multiplier_1_out), .out(out_4), .sel(H));
endmodule

module BC (
);

  main main_1 ();  // open: A, B, LH, C, M1, clkH, RSTH, M0, H, X, LS, LX, clkS, M2, RST, out_16, Pronto, out_18
endmodule
